// Logisim project BasemARMiFA21154aV002.circ as structural Verilog: 3 circuits, main circuit main
module main (
);

  wire clock_1_out, cpu_1_halt, frontpanelcontroller_1_cpuclk, frontpanelcontroller_1_runhalt, Reset_out,
       RunStop_out, Step_out, undriven, undriven_2, undriven_3, undriven_4, undriven_5, undriven_6,
       undriven_7, undriven_8;
  wire [3:0] cpu_1_aluflags, cpu_1_flags;
  wire [15:0] cpu_1_alua, cpu_1_alub, cpu_1_aluresult, cpu_1_dmaddress, cpu_1_dmdata, cpu_1_imaddress,
       cpu_1_imdata, cpu_1_writeback, IM_data;

  Clock clock_1 (.out(clock_1_out));
  ROM #(.addrWidth(16), .dataWidth(16)) IM (.addr(cpu_1_imaddress), .data(IM_data));
  FrontPanelController frontpanelcontroller_1 (
    .Clk(clock_1_out), .Run(RunStop_out), .Step(Step_out), .Reset(Reset_out), .Halt(cpu_1_halt),
    .CpuClk(frontpanelcontroller_1_cpuclk), .RunHalt(frontpanelcontroller_1_runhalt));
  CPU cpu_1 (
    .CLK(frontpanelcontroller_1_cpuclk), .Reset(Reset_out), .IMDataIn(IM_data), .Halt(cpu_1_halt),
    .IMAddress(cpu_1_imaddress), .IMData(cpu_1_imdata), .DMAddress(cpu_1_dmaddress), .DMData(cpu_1_dmdata),
    .WriteBack(cpu_1_writeback), .Flags(cpu_1_flags), .AluA(cpu_1_alua), .AluB(cpu_1_alub),
    .ALUResult(cpu_1_aluresult), .ALUFlags(cpu_1_aluflags));
  LED led_1 (.in(cpu_1_flags[2]));
  LED led_2 (.in(cpu_1_flags[3]));
  LED led_3 (.in(cpu_1_flags[0]));
  LED led_4 (.in(cpu_1_flags[1]));
  Hex_Digit_Display hex_digit_display_1 (.value(cpu_1_alua[15:12]));  // open: dp
  LED led_5 (.in(cpu_1_halt));
  Hex_Digit_Display hex_digit_display_2 (.value(cpu_1_imaddress[11:8]), .dp(undriven_2));
  Hex_Digit_Display hex_digit_display_3 (.value(cpu_1_imaddress[11:8]), .dp(undriven_2));
  Hex_Digit_Display hex_digit_display_4 (.value(cpu_1_imaddress[15:12]));  // open: dp
  Hex_Digit_Display hex_digit_display_5 (.value(cpu_1_imdata[11:8]), .dp(undriven_3));
  Hex_Digit_Display hex_digit_display_6 (.value(cpu_1_imdata[11:8]), .dp(undriven_3));
  Hex_Digit_Display hex_digit_display_7 (.value(cpu_1_imdata[15:12]));  // open: dp
  Hex_Digit_Display hex_digit_display_8 (.value(cpu_1_alua[11:8]), .dp(undriven));
  Hex_Digit_Display hex_digit_display_9 (.value(cpu_1_alua[11:8]), .dp(undriven));
  Hex_Digit_Display hex_digit_display_10 (.value(cpu_1_alua[7:4]));  // open: dp
  LED N (.in(cpu_1_aluflags[3]));
  LED Z (.in(cpu_1_aluflags[2]));
  LED C (.in(cpu_1_aluflags[1]));
  Button RunStop (.out(RunStop_out));
  LED led_6 (.in(frontpanelcontroller_1_runhalt));
  Hex_Digit_Display hex_digit_display_11 (.value(cpu_1_imaddress[3:0]));  // open: dp
  Hex_Digit_Display hex_digit_display_12 (.value(cpu_1_imaddress[7:4]));  // open: dp
  // Hex_Digit_Display hex_digit_display_13: pin names not known; wires that end beside it: cpu_1_imdata[3:0]
  Hex_Digit_Display hex_digit_display_14 (.value(cpu_1_imdata[7:4]));  // open: dp
  Hex_Digit_Display hex_digit_display_15 (.value(cpu_1_alua[3:0]));  // open: dp
  LED V (.in(cpu_1_aluflags[0]));
  Button Step (.out(Step_out));
  Hex_Digit_Display hex_digit_display_16 (.value(cpu_1_dmaddress[15:12]));  // open: dp
  Hex_Digit_Display hex_digit_display_17 (.value(cpu_1_dmdata[15:12]));  // open: dp
  Hex_Digit_Display hex_digit_display_18 (.value(cpu_1_writeback[15:12]));  // open: dp
  Hex_Digit_Display hex_digit_display_19 (.value(cpu_1_alub[15:12]));  // open: dp
  Hex_Digit_Display hex_digit_display_20 (.value(cpu_1_aluresult[15:12]));  // open: dp
  Button Reset (.out(Reset_out));
  Hex_Digit_Display hex_digit_display_21 (.value(cpu_1_dmaddress[7:4]));  // open: dp
  Hex_Digit_Display hex_digit_display_22 (.value(cpu_1_dmaddress[11:8]), .dp(undriven_4));
  Hex_Digit_Display hex_digit_display_23 (.value(cpu_1_dmaddress[11:8]), .dp(undriven_4));
  Hex_Digit_Display hex_digit_display_24 (.value(cpu_1_dmdata[7:4]));  // open: dp
  Hex_Digit_Display hex_digit_display_25 (.value(cpu_1_dmdata[11:8]), .dp(undriven_5));
  Hex_Digit_Display hex_digit_display_26 (.value(cpu_1_dmdata[11:8]), .dp(undriven_5));
  Hex_Digit_Display hex_digit_display_27 (.value(cpu_1_writeback[7:4]));  // open: dp
  Hex_Digit_Display hex_digit_display_28 (.value(cpu_1_writeback[11:8]), .dp(undriven_6));
  Hex_Digit_Display hex_digit_display_29 (.value(cpu_1_writeback[11:8]), .dp(undriven_6));
  Hex_Digit_Display hex_digit_display_30 (.value(cpu_1_alub[11:8]), .dp(undriven_7));
  Hex_Digit_Display hex_digit_display_31 (.value(cpu_1_alub[11:8]), .dp(undriven_7));
  Hex_Digit_Display hex_digit_display_32 (.value(cpu_1_alub[7:4]));  // open: dp
  Hex_Digit_Display hex_digit_display_33 (.value(cpu_1_aluresult[7:4]));  // open: dp
  Hex_Digit_Display hex_digit_display_34 (.value(cpu_1_aluresult[11:8]), .dp(undriven_8));
  Hex_Digit_Display hex_digit_display_35 (.value(cpu_1_aluresult[11:8]), .dp(undriven_8));
  Hex_Digit_Display hex_digit_display_36 (.value(cpu_1_dmaddress[3:0]));  // open: dp
  Hex_Digit_Display hex_digit_display_37 (.value(cpu_1_dmdata[3:0]));  // open: dp
  Hex_Digit_Display hex_digit_display_38 (.value(cpu_1_writeback[3:0]));  // open: dp
  Hex_Digit_Display hex_digit_display_39 (.value(cpu_1_alub[3:0]));  // open: dp
  Hex_Digit_Display hex_digit_display_40 (.value(cpu_1_aluresult[3:0]));  // open: dp

  // Notes on the sheet:
  //   N  Z  C  V
  //   Latched Flags
  //   HALT
  //   Instruction Memory
  //   mARMi
  //   ALU A Input
  //   ALU Flags
  //   Data Memory
  //   WriteBack
  //   ALU B Input
  //   ALU Result
endmodule

module CPU (
  input  CLK,
  input  Reset,
  input  [15:0] IMDataIn,
  output Halt,
  output [15:0] IMAddress,
  output [15:0] IMData,
  output [15:0] DMAddress,
  output [15:0] DMData,
  output [15:0] WriteBack,
  output [3:0] Flags,
  output [15:0] AluA,
  output [15:0] AluB,
  output [15:0] ALUResult,
  output [3:0] ALUFlags
);


  assign IMData = IMDataIn;

  // Other names for the same wires on the sheet: A[15:0] = AluA; B[15:0] = AluB; CLKin = CLK;
  //   Result[15:0] = ALUResult

  // Notes on the sheet:
  //   Build your CPU here
endmodule

module FrontPanelController (
  input  Clk,
  input  Run,
  input  Step,
  input  Reset,
  input  Halt,
  output CpuClk,
  output RunHalt
);

  wire and_1_out, or_1_out, pull_resistor_1_node, t_ff_1_q;

  T_Flip_Flop t_ff_1 (.T(pull_resistor_1_node), .clk(Run), .Q(t_ff_1_q), .reset(Reset));  // open: Qn, preset
  Pull_Resistor #(.pull(1)) pull_resistor_1 (.node(pull_resistor_1_node));
  or or_1 (or_1_out, t_ff_1_q, Step);
  and and_1 (and_1_out, Clk, t_ff_1_q);
  and and_2 (RunHalt, or_1_out, ~Halt);  // AND_Gate
  Multiplexer #(.enable("false")) multiplexer_1 (.in0(Step), .in1(and_1_out), .out(CpuClk), .sel(t_ff_1_q));
endmodule
