// Logisim project umips.circ as structural Verilog: 3 circuits, main circuit main
module main (
  output [15:0] Reg0,
  output [15:0] Reg1,
  output [15:0] Reg2,
  output [15:0] Reg3,
  output [15:0] Reg4,
  output [15:0] Reg5,
  output [15:0] Reg6,
  output [15:0] Reg7,
  output [3:0] Output3,
  output [3:0] Output2,
  output [3:0] Output1,
  output [3:0] Output0,
  output halt
);

  wire AddZero, ALUSrc, BranchTrue, Clock, control_1_regwrite, control_1_regwriteb, JAL, JR, Jump, main_2_gt,
       main_2_lt, main_2_zero, MemToReg, MemWrite, not_1_p1, not_2_p1, or_1_out, put, Subop;
  wire [1:0] multiplexer_1_p4;
  wire [2:0] ALUOp, BranchCase, Rs;
  wire [7:0] Immediate, multiplexer_1_p6, PC_1, register_1_q;
  wire [15:0] bit_extender_1_out, bit_extender_2_out, bit_extender_3_out, DataA, DataB, main_2_result,
       multiplexer_2_out, multiplexer_3_out, multiplexer_4_out, multiplexer_5_out, multiplexer_6_out,
       multiplexer_7_out, R2, ram_1_data;
  wire [15:12] rom_1_data;

  Adder adder_1 (.a(register_1_q), .b(8'h1), .out(PC_1));  // open: cin, cout
  or or_1 (or_1_out, Jump, JAL, BranchTrue);
  // Multiplexer #(.select(2), .width(8), .disabled(0)) multiplexer_1: pin names not known; wires that end beside it: PC_1, Immediate, DataA[7:0], multiplexer_1_p4, multiplexer_1_p4, multiplexer_1_p6, halt
  // NOT_Gate not_1: pin names not known; wires that end beside it: not_1_p1, halt
  Priority_Encoder #(.select(2)) priority_encoder_1 (
    .in0(1'b1), .in1(or_1_out), .in2(JR), .out(multiplexer_1_p4));  // open: in3, gs, en_out, en_in
  Register register_1 (.D(multiplexer_1_p6), .en(not_1_p1), .Q(register_1_q), .clk(Clock));  // open: clr
  Clock clock_1 (.out(Clock));
  // NOT_Gate not_2: pin names not known; wires that end beside it: not_2_p1, halt
  ROM #(.dataWidth(16)) rom_1 (.addr(register_1_q), .data({rom_1_data, Rs, Immediate, Subop}), .sel(not_2_p1));
  Control control_1 (
    .Opcode(rom_1_data), .ALUop(ALUOp), .Jump(Jump), .MemToReg(MemToReg), .MemWrite(MemWrite),
    .ALUSrc(ALUSrc), .Subop(Subop), .Halt(halt), .Put(put), .RegWrite(control_1_regwrite),
    .RegWriteB(control_1_regwriteb), .AddZero(AddZero), .JR(JR), .Jal(JAL), .BranchCase(BranchCase));
  assign bit_extender_1_out = {{8{1'b0}}, PC_1};  // Bit_Extender bit_extender_1
  Multiplexer #(.width(16)) multiplexer_2 (
    .in0(multiplexer_7_out), .in1(bit_extender_1_out), .out(multiplexer_2_out), .sel(JAL));  // open: en
  // Probe on Rs
  // Probe on Immediate[7:5]
  // Probe on Immediate
  assign bit_extender_2_out = {{8{1'b0}}, Immediate};  // Bit_Extender bit_extender_2
  assign bit_extender_3_out = {{8{Immediate[7]}}, Immediate};  // Bit_Extender bit_extender_3
  RegFile_main main_1 (
    .WriteData0(multiplexer_2_out), .WriteData1(R2), .ReadData0(DataA), .ReadData1(DataB), .WriteSelect0(Rs),
    .ReadSelect0(Rs), .ReadSelect1(Immediate[7:5]), .Reg0(Reg0), .Reg1(Reg1), .Reg2(Reg2), .Reg3(Reg3),
    .Reg4(Reg4), .Reg5(Reg5), .Reg6(Reg6), .Reg7(Reg7), .WE0(control_1_regwrite), .WE1(control_1_regwriteb),
    .Clock(Clock));
  // Probe on DataA
  // Probe on multiplexer_3_out
  Multiplexer #(.width(16)) multiplexer_3 (
    .in0(bit_extender_2_out), .in1(bit_extender_3_out), .out(multiplexer_3_out), .sel(Subop));  // open: en
  Register #(.width(16)) register_2 (
    .D(DataA), .en(put), .Q({Output3, Output2, Output1, Output0}), .clk(Clock));  // open: clr
  Multiplexer #(.width(16)) multiplexer_4 (
    .in0(DataA), .in1({16{1'b0}}), .out(multiplexer_4_out), .sel(AddZero));  // open: en
  ALU_main main_2 (
    .ALUOp(ALUOp), .A(multiplexer_4_out), .B(multiplexer_6_out), .Result(main_2_result), .GT(main_2_gt),
    .Zero(main_2_zero), .LT(main_2_lt), .Result2(R2));
  Multiplexer #(.width(16)) multiplexer_5 (
    .in0(DataB), .in1(multiplexer_3_out), .out(multiplexer_5_out), .sel(ALUSrc));  // open: en
  Multiplexer #(.width(16)) multiplexer_6 (
    .in0(multiplexer_5_out), .in1({16{1'b0}}), .out(multiplexer_6_out), .sel(MemWrite));  // open: en
  Hex_Digit_Display hex_digit_display_1 (.value(Output2));  // open: dp
  Hex_Digit_Display hex_digit_display_2 (.value(Output3));  // open: dp
  // Probe on ALUOp
  Hex_Digit_Display hex_digit_display_3 (.value(Output1));  // open: dp
  Hex_Digit_Display hex_digit_display_4 (.value(Output0));  // open: dp
  // Probe on main_2_result
  // Probe on R2
  BranchControl branchcontrol_1 (
    .BranchCase(BranchCase), .GT(main_2_gt), .Z(main_2_zero), .LT(main_2_lt), .BranchTrue(BranchTrue));
  LED led_1 (.in(halt));
  // Probe on multiplexer_7_out
  Multiplexer #(.width(16)) multiplexer_7 (
    .in0(main_2_result), .in1(ram_1_data), .out(multiplexer_7_out), .sel(MemToReg));  // open: en
  RAM #(.dataWidth(16), .bus("separate")) ram_1 (
    .addr(DataB[7:0]), .din(main_2_result), .data(ram_1_data), .str(MemWrite), .clk(Clock), .ld(MemToReg));  // open: sel, clr

  // Other names for the same wires on the sheet: Rt[2:0] = Immediate[7:5]

  // Notes on the sheet:
  //   Increments PC
  //   Program Counter
  //   contents of rom_1 (hex, n*v repeats v):
  //   500a 540a 300a 2000 7000 7001
  //   Opcode
  //    Don't modify these, they are used for debug and testing
  //   Design your CPU in this file
  //   You must connect Reg0..7 to the top ports of the register file.
  //   Zero extend
  //   Sign extend
  //   Include everything here (ALU, RegFile, Control, PC, RAM, ROM, LEDs, Displays, ...)
  //   Connect Output3..0 to your LED display.
  //   Output3 is the most significant
  //   Connect halt to your halt LED
endmodule

module Control (
  input  [3:0] Opcode,
  input  Subop,
  output [2:0] ALUop,
  output Halt,
  output Put,
  output Jump,
  output JR,
  output Jal,
  output MemToReg,
  output MemWrite,
  output AddZero,
  output ALUSrc,
  output [2:0] BranchCase,
  output RegWrite,
  output RegWriteB
);

  wire ADD, ADDI, ADDUI, AND, BN, BP, BX, BZ, decoder_1_out8, decoder_1_out9, decoder_1_out16,
       decoder_1_out17, decoder_1_out18, decoder_1_out19, decoder_1_out20, decoder_1_out21, decoder_1_out22,
       decoder_1_out23, decoder_1_out24, decoder_1_out25, decoder_1_out26, decoder_1_out27, decoder_1_out28,
       decoder_1_out29, decoder_1_out30, decoder_1_out31, DIV, LI, MUL, NOR, or_11_out, SLLV, SRLV, SUB;

  Decoder #(.select(5)) decoder_1 (
    .out0(ADD), .out1(SUB), .out2(NOR), .out3(AND), .out4(MUL), .out5(DIV), .out6(ADDUI), .out7(ADDI),
    .out8(decoder_1_out8), .out9(decoder_1_out9), .out10(LI), .out12(SRLV), .out13(SLLV), .out14(MemWrite),
    .out15(MemToReg), .out16(decoder_1_out16), .out17(decoder_1_out17), .out18(decoder_1_out18),
    .out19(decoder_1_out19), .out20(decoder_1_out20), .out21(decoder_1_out21), .out22(decoder_1_out22),
    .out23(decoder_1_out23), .out24(decoder_1_out24), .out25(decoder_1_out25), .out26(decoder_1_out26),
    .out27(decoder_1_out27), .out28(decoder_1_out28), .out29(decoder_1_out29), .out30(decoder_1_out30),
    .out31(decoder_1_out31), .sel({Opcode, Subop}));  // open: out11, en
  or or_1 (AddZero, LI, Jump);
  Priority_Encoder priority_encoder_1 (
    .in0(1'b1), .in1(BP), .in2(BN), .in3(BX), .in4(BZ), .out(BranchCase));  // open: in5, in6, in7, en_in, gs, en_out
  or or_2 (BP, decoder_1_out8, decoder_1_out9);
  or or_3 (Put, decoder_1_out16, decoder_1_out16, decoder_1_out17);
  // OR_Gate or_4: pin names not known; wires that end beside it: decoder_1_out18, Halt, decoder_1_out19
  or or_5 (Jal, decoder_1_out20, decoder_1_out21);
  // OR_Gate or_6: pin names not known; wires that end beside it: decoder_1_out22, Jump, decoder_1_out23
  // OR_Gate or_7: pin names not known; wires that end beside it: decoder_1_out24, BN, decoder_1_out25
  // OR_Gate or_8: pin names not known; wires that end beside it: decoder_1_out26, BX, decoder_1_out27
  or or_9 (JR, decoder_1_out28, decoder_1_out28, decoder_1_out29);
  // OR_Gate or_10: pin names not known; wires that end beside it: decoder_1_out30, decoder_1_out31, decoder_1_out31, BZ
  or or_11 (or_11_out, LI, ADD, ADDI, MemToReg, MemWrite, ADDUI);
  or or_12 (ALUSrc, ADDI, ADDUI, LI, Jump);
  or or_13 (RegWrite, Jal, LI, MUL, ADDI, AND, NOR, ADD, SUB, SRLV, MemToReg, DIV, ADDUI, SLLV);
  Priority_Encoder priority_encoder_2 (
    .in0(AND), .in1(NOR), .in2(or_11_out), .in3(SUB), .in4(MUL), .in5(DIV), .in6(SLLV), .in7(SRLV),
    .out(ALUop));  // open: en_in, gs, en_out
  or or_14 (RegWriteB, MUL, DIV);

  // Other names for the same wires on the sheet: J = Jump; LW = MemToReg; SW = MemWrite
endmodule

module BranchControl (
  input  [2:0] BranchCase,
  input  GT,
  input  Z,
  input  LT,
  output BranchTrue
);

  wire and_1_out, and_2_out, and_3_out, and_4_out, BEQZ, BNEZ, BranchIfNeg, BranchIfPos, not_1_p2;

  // Decoder #(.select(3)) decoder_1: pin names not known; wires that end beside it: BranchCase, BranchIfPos, BranchIfNeg, BNEZ, BEQZ
  // NOT_Gate not_1: pin names not known; wires that end beside it: Z, not_1_p2
  and and_1 (and_1_out, BranchIfPos, GT);
  and and_2 (and_2_out, BNEZ, not_1_p2);
  and and_3 (and_3_out, Z, BEQZ);
  and and_4 (and_4_out, LT, BranchIfNeg);
  or or_1 (BranchTrue, and_1_out, and_2_out, and_3_out, and_4_out);
endmodule
